// Logisim project dflipflopen.circ as structural Verilog: 1 circuit, main circuit main
module main (
  input  WD,
  input  WD_2,
  input  D,
  input  D_2,
  input  CLK,
  input  in_6,
  input  in_7,
  input  in_8,
  input  in_9,
  output Q,
  output Q_2,
  output QN,
  output QN_2,
  output out_14,
  output out_15
);

  wire clock_1_out, clock_2_out, clock_3_out, nand_1_out, nand_2_out, nand_3_out, nand_4_out, nand_5_out,
       not_1_out, not_2_out, pull_resistor_1_node, pull_resistor_4_node, pull_resistor_5_node,
       pull_resistor_6_node, pull_resistor_9_node, pull_resistor_10_node, pull_resistor_11_node,
       pull_resistor_13_node, pull_resistor_19_node, pull_resistor_20_node, pull_resistor_23_node,
       transistor_2_out, transistor_3_out, transistor_4_out, transistor_7_out, transistor_8_out,
       transistor_9_out, transistor_11_out, transistor_12_out, transistor_13_out, transistor_14_out,
       transistor_16_out, transistor_18_out, transistor_20_out, transistor_22_out, transistor_24_out,
       transistor_26_out, transistor_27_out, transistor_29_out, transistor_30_out, transistor_31_out,
       transistor_34_out, transistor_35_out, transistor_37_out, transistor_38_out, transistor_39_out,
       transistor_41_out, transistor_43_out;

  Pull_Resistor #(.pull(1)) pull_resistor_1 (.node(pull_resistor_1_node));
  Transistor #(.\type ("n")) transistor_1 (.in(1'b0), .out(pull_resistor_1_node), .gate(WD));
  Transistor #(.\type ("n")) transistor_2 (.in(transistor_3_out), .out(transistor_2_out), .gate(WD));
  Pull_Resistor #(.pull(1)) pull_resistor_2 (.node(transistor_2_out));
  Transistor #(.\type ("n")) transistor_3 (.in(1'b0), .out(transistor_3_out), .gate(D_2));
  Clock clock_1 (.out(clock_1_out));
  Transistor #(.\type ("n"), .gate("br")) transistor_4 (.in(transistor_8_out), .out(transistor_4_out), .gate(in_9));
  Pull_Resistor #(.pull(1)) pull_resistor_3 (.node(transistor_4_out));
  Pull_Resistor #(.pull(1)) pull_resistor_4 (.node(pull_resistor_4_node));
  Transistor #(.\type ("n")) transistor_5 (.in(1'b0), .out(pull_resistor_4_node), .gate(transistor_13_out));
  Pull_Resistor #(.pull(1)) pull_resistor_5 (.node(pull_resistor_5_node));
  Transistor #(.\type ("n")) transistor_6 (.in(transistor_7_out), .out(pull_resistor_5_node), .gate(Q));
  Transistor #(.\type ("n")) transistor_7 (.in(1'b0), .out(transistor_7_out), .gate(pull_resistor_1_node));
  Transistor #(.\type ("n"), .gate("br")) transistor_8 (.in(1'b0), .out(transistor_8_out), .gate(in_8));
  Transistor #(.\type ("n")) transistor_9 (.in(1'b0), .out(transistor_9_out), .gate(pull_resistor_4_node));
  Pull_Resistor #(.pull(1)) pull_resistor_6 (.node(pull_resistor_6_node));
  Transistor #(.\type ("n")) transistor_10 (
    .in(transistor_11_out), .out(pull_resistor_6_node), .gate(pull_resistor_5_node));
  Transistor #(.\type ("n")) transistor_11 (.in(1'b0), .out(transistor_11_out), .gate(transistor_2_out));
  Transistor #(.\type ("n"), .gate("br")) transistor_12 (.in(1'b0), .out(transistor_12_out), .gate(transistor_20_out));
  Transistor #(.\type ("n"), .gate("br")) transistor_13 (
    .in(transistor_12_out), .out(transistor_13_out), .gate(transistor_4_out));
  Pull_Resistor #(.pull(1)) pull_resistor_7 (.node(transistor_13_out));
  Transistor #(.\type ("n")) transistor_14 (.in(transistor_9_out), .out(transistor_14_out), .gate(clock_2_out));
  Pull_Resistor #(.pull(1)) pull_resistor_8 (.node(transistor_14_out));
  Pull_Resistor #(.pull(1)) pull_resistor_9 (.node(pull_resistor_9_node));
  Transistor #(.\type ("n")) transistor_15 (
    .in(transistor_16_out), .out(pull_resistor_9_node), .gate(pull_resistor_6_node));
  Transistor #(.\type ("n")) transistor_16 (.in(1'b0), .out(transistor_16_out), .gate(clock_1_out));
  Pull_Resistor #(.pull(1)) pull_resistor_10 (.node(pull_resistor_10_node));
  Transistor #(.\type ("n")) transistor_17 (.in(transistor_18_out), .out(pull_resistor_10_node), .gate(clock_1_out));
  Transistor #(.\type ("n")) transistor_18 (.in(1'b0), .out(transistor_18_out), .gate(pull_resistor_11_node));
  Pull_Resistor #(.pull(1)) pull_resistor_11 (.node(pull_resistor_11_node));
  Transistor #(.\type ("n")) transistor_19 (.in(1'b0), .out(pull_resistor_11_node), .gate(pull_resistor_6_node));
  Transistor #(.\type ("n"), .gate("br")) transistor_20 (
    .in(transistor_27_out), .out(transistor_20_out), .gate(out_15));
  Pull_Resistor #(.pull(1)) pull_resistor_12 (.node(transistor_20_out));
  Pull_Resistor #(.pull(1)) pull_resistor_13 (.node(pull_resistor_13_node));
  Transistor #(.\type ("n")) transistor_21 (.in(transistor_22_out), .out(pull_resistor_13_node), .gate(clock_2_out));
  Transistor #(.\type ("n")) transistor_22 (.in(1'b0), .out(transistor_22_out), .gate(transistor_13_out));
  Pull_Resistor #(.pull(1)) pull_resistor_14 (.node(Q));
  Transistor #(.\type ("n")) transistor_23 (.in(transistor_24_out), .out(Q), .gate(pull_resistor_9_node));
  Transistor #(.\type ("n")) transistor_24 (.in(1'b0), .out(transistor_24_out), .gate(QN));
  Pull_Resistor #(.pull(1)) pull_resistor_15 (.node(QN));
  Transistor #(.\type ("n")) transistor_25 (.in(transistor_26_out), .out(QN), .gate(Q));
  Transistor #(.\type ("n")) transistor_26 (.in(1'b0), .out(transistor_26_out), .gate(pull_resistor_10_node));
  Transistor #(.\type ("n"), .gate("br")) transistor_27 (.in(1'b0), .out(transistor_27_out), .gate(transistor_30_out));
  Pull_Resistor #(.pull(1)) pull_resistor_16 (.node(pull_resistor_13_node));
  Transistor #(.\type ("n")) transistor_28 (.in(transistor_29_out), .out(pull_resistor_13_node), .gate(out_15));
  Transistor #(.\type ("n")) transistor_29 (.in(1'b0), .out(transistor_29_out), .gate(transistor_14_out));
  Transistor #(.\type ("n"), .gate("br")) transistor_30 (.in(1'b0), .out(transistor_30_out), .gate(in_9));
  Pull_Resistor #(.pull(1)) pull_resistor_17 (.node(transistor_30_out));
  Transistor #(.\type ("n")) transistor_31 (.in(1'b0), .out(transistor_31_out), .gate(pull_resistor_13_node));
  Clock clock_2 (.out(clock_2_out));
  Transistor #(.\type ("n")) transistor_32 (.in(transistor_31_out), .out(out_15), .gate(pull_resistor_13_node));
  Pull_Resistor #(.pull(1)) pull_resistor_18 (.node(out_15));
  Pull_Resistor #(.pull(1)) pull_resistor_19 (.node(pull_resistor_19_node));
  Transistor #(.\type ("n"), .gate("br")) transistor_33 (
    .in(transistor_34_out), .out(pull_resistor_19_node), .gate(in_7));
  nand nand_1 (nand_1_out, Q_2, not_1_out);
  not not_1 (not_1_out, WD_2);
  nand nand_2 (nand_2_out, WD_2, D);
  Transistor #(.\type ("n"), .gate("br")) transistor_34 (.in(1'b0), .out(transistor_34_out), .gate(in_6));
  Transistor #(.\type ("n"), .gate("br")) transistor_35 (.in(1'b0), .out(transistor_35_out), .gate(transistor_37_out));
  Pull_Resistor #(.pull(1)) pull_resistor_20 (.node(pull_resistor_20_node));
  Transistor #(.\type ("n"), .gate("br")) transistor_36 (
    .in(transistor_35_out), .out(pull_resistor_20_node), .gate(pull_resistor_19_node));
  nand nand_3 (nand_3_out, nand_1_out, nand_2_out);
  not not_2 (not_2_out, nand_3_out);
  Transistor #(.\type ("n"), .gate("br")) transistor_37 (.in(1'b0), .out(transistor_37_out), .gate(out_14));
  Pull_Resistor #(.pull(1)) pull_resistor_21 (.node(transistor_37_out));
  Transistor #(.\type ("n")) transistor_38 (.in(1'b0), .out(transistor_38_out), .gate(clock_3_out));
  Pull_Resistor #(.pull(1)) pull_resistor_22 (.node(transistor_38_out));
  nand nand_4 (nand_4_out, nand_3_out, CLK);
  nand nand_5 (nand_5_out, not_2_out, CLK);
  Transistor #(.\type ("n")) transistor_39 (.in(1'b0), .out(transistor_39_out), .gate(pull_resistor_20_node));
  nand nand_6 (Q_2, nand_4_out, QN_2);
  nand nand_7 (QN_2, Q_2, nand_5_out);
  Pull_Resistor #(.pull(1)) pull_resistor_23 (.node(pull_resistor_23_node));
  Transistor #(.\type ("n")) transistor_40 (.in(transistor_39_out), .out(pull_resistor_23_node), .gate(clock_3_out));
  Transistor #(.\type ("n")) transistor_41 (.in(1'b0), .out(transistor_41_out), .gate(transistor_38_out));
  Clock clock_3 (.out(clock_3_out));
  Pull_Resistor #(.pull(1)) pull_resistor_24 (.node(pull_resistor_23_node));
  Transistor #(.\type ("n")) transistor_42 (.in(transistor_41_out), .out(pull_resistor_23_node), .gate(out_14));
  Transistor #(.\type ("n")) transistor_43 (.in(1'b0), .out(transistor_43_out), .gate(pull_resistor_23_node));
  Transistor #(.\type ("n")) transistor_44 (.in(transistor_43_out), .out(out_14), .gate(pull_resistor_23_node));
  Pull_Resistor #(.pull(1)) pull_resistor_25 (.node(out_14));
endmodule
